# Fritzing sketch schemas (saved by Fritzing 1.0.1rc)
breadboards: 1

parts:
  BAT1 = Battery Holders [package=lipo-1100mAh]
  RFID_reader_RC522 = RFID-RC522-v2
  SparkFun_ESP32_Thing_Plus1 = SparkFun ESP32 Thing Plus [part_number=14689]
  Vibror_motor_Grove = Vibration sensor module

nets:
  N1: BAT1.+, SparkFun_ESP32_Thing_Plus1.V_BATT, Vibror_motor_Grove.vcc
  GND: BAT1.-, RFID_reader_RC522.GND, SparkFun_ESP32_Thing_Plus1.GND, Vibror_motor_Grove.Ground
  N2: RFID_reader_RC522.SDA, SparkFun_ESP32_Thing_Plus1.SDA
  N3: RFID_reader_RC522.SCK, SparkFun_ESP32_Thing_Plus1.SCK
  N4: RFID_reader_RC522.MOSI, SparkFun_ESP32_Thing_Plus1.MOSI
  N5: RFID_reader_RC522.MISO, SparkFun_ESP32_Thing_Plus1.MISO
  N6: RFID_reader_RC522.RST, SparkFun_ESP32_Thing_Plus1.12
  3.3V: RFID_reader_RC522.3.3V, SparkFun_ESP32_Thing_Plus1.3.3V
  N7: SparkFun_ESP32_Thing_Plus1.33, Vibror_motor_Grove.Digital_output

custom parts:
  RFID-RC522-v2: A simple China made RFID-RC522 Reader; do check the pin labels, as this is a MFRC522 based clone.
  SparkFun ESP32 Thing Plus: The SparkFun ESP32 Thing Plus enjoys all the amenities of the ESP32 Thing, but with a few added sparkles. We've lengthened the board just a bit to accommodate a Qwiic connector for all your Qwiic breakout needs. We've also moved a few pins around to make the board compatible with the Adafruit Huzzah32 – ESP32 Feather Board such that you can use all of those lovely shields available out there!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
  Vibration sensor module: Single-roller type full induction trigger switch. When no vibration or tilt, the product is ON conduction state, and in the steady state, when a vibration or tilt, the switch will be rendered instantly disconnect the conductive resistance increases, generating a current pulse signal, thereby triggering circuit. The default state of the swith is close Digital output Supply voltage:3.3V-5V On-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
